# Fritzing sketch puzzlebox (saved by Fritzing 0.9.2b)
circuit board: 8.46667cm x 5.64444cm
breadboards: 1

parts:
  atmega328p-pu = atmega328 [package=dip]
  Trellis = Adafruit Trellis
  Resonator = Resonator [frequency="16 Mhz" package=THT]
  USB = USB Connectors [package=usb-b-pth-vertical]

nets:
  VCC: atmega328p-pu.VCC, atmega328p-pu.AVCC, Trellis.5V, USB.VBUS
  GND: atmega328p-pu.GND, Trellis.GND, Resonator.GND, USB.GND
  N1: atmega328p-pu.XLAT1, Resonator.0
  N2: atmega328p-pu.XLAT2, Resonator.pin_1
  N3: atmega328p-pu.A2, Trellis.INT
  N4: atmega328p-pu.A4, Trellis.SDA
  N5: atmega328p-pu.A5, Trellis.SCL
